# Fritzing sketch Schaltplan (saved by Fritzing 0.9.3b)
breadboards: 1

parts:
  U1 = ATTiny84 [package=dip]
  LED1 = LED - 5mm [color="Red (633nm)" package="5 mm [THT]"]
  R1 = Resistor [tolerance=±5% resistance=220 package=THT]
  HC-SR04_Sensor_1 = HC-SR04 Ultrasonic Distance Sensor
  VCC1 = Battery

nets:
  N1: U1.pin1, HC-SR04_Sensor_1.VCC, VCC1.+
  N2: U1.pin2, HC-SR04_Sensor_1.ECHO
  N3: U1.pin3, HC-SR04_Sensor_1.TRIG
  N4: U1.pin6, LED1.cathode
  N5: U1.pin14, R1.Pin_1, HC-SR04_Sensor_1.GND, VCC1.-
  N6: LED1.anode, R1.Pin_0

custom parts:
  ATTiny84: Atmel ATTiny84 processor. 8 ADC pins, 4 PWM pins. Available in either 10MHz or 20MHz. The last 2 pin numbers refer to arduino. D6 = Arduino 6, A6 = Arduino A6 example: PA6 (SDA/MOSI/OC1A/DI/AD6/PCINT6/D6/A6) NOTE: This part is diagrammed to suit the MIT HLT ATTiny84 core at https://github.com/damellis/attiny/
